// Logisim project CPU RiscV SIMD.circ as structural Verilog
module main (
  input  in_1
);

  wire alu_1_f_zero, alu_control_1_beq_bne, and_1_out, and_2_out, and_3_out, clock_1_out,
       control_unit_1_alu_src, control_unit_1_branch, control_unit_1_jump_reg, control_unit_1_mem_read,
       control_unit_1_mem_to_reg, control_unit_1_mem_write, control_unit_1_mode, control_unit_1_reg_write,
       control_unit_1_soma_pc, exmem_1_branch_out, exmem_1_jalr_ou_jal_out, exmem_1_mem_read_out,
       exmem_1_mem_to_reg_out, exmem_1_mem_write_out, exmem_1_reg_write_out, exmem_1_zero_out,
       hazard_1_stall, idex_1_alu_src_out, idex_1_branch_out, idex_1_jumpreg_out, idex_1_mem_read_out,
       idex_1_mem_to_reg_out, idex_1_mem_write_out, idex_1_mode_out, idex_1_reg_write_out,
       idex_1_soma_pc_out, memwb_1_mem_to_reg_out, memwb_1_reg_write_out, not_1_out, not_2_out, or_1_out;
  wire [1:0] control_unit_1_alu_op, control_unit_1_vector_size, forward_1_forward_a, forward_1_forward_b,
       idex_1_alu_op_out, idex_1_vector_size_out;
  wire [2:0] control_unit_1_s_funct3, idex_1_funct3_out;
  wire [3:0] alu_control_1_alu_out;
  wire [4:0] exmem_1_rd_out, idex_1_rd_out, idex_1_rs1_out, idex_1_rs2_out, ifid_1_rd, ifid_1_rs1,
       ifid_1_rs2, memwb_1_rd_out;
  wire [6:0] control_unit_1_s_funct7, control_unit_1_s_opcode, idex_1_funct7_out, idex_1_opcode_out;
  wire [23:0] exmem_1_alu_result_out;
  wire [31:0] alu_1_result, exmem_1_new_pc_out, exmem_1_read2_out, idex_1_immediate_out, idex_1_pc_out,
       idex_1_read1_out, idex_1_read2_out, ifid_1_instruction_out, ifid_1_pc_out, immgen_1_immediate,
       memwb_1_alu_result_out, memwb_1_mem_data_out, multiplexer_1_out, multiplexer_2_out, multiplexer_3_out,
       multiplexer_4_out, multiplexer_5_out, multiplexer_6_out, multiplexer_8_out, pc4_1_pc_out, ram_1_dout,
       registerfile_1_read_data_1, registerfile_1_read_data_2, rom_1_data, somador_1_z;
  wire [31:24] exmem_1_alu_result_out_2;

  Clock clock_1 (.out(clock_1_out));
  Multiplexer #(.width(32)) multiplexer_1 (
    .in0(pc4_1_pc_out), .in1(exmem_1_new_pc_out), .out(multiplexer_1_out), .sel(or_1_out));
  PC4 pc4_1 (
    .clk(clock_1_out), .reset(in_1), .PC_in(multiplexer_1_out), .Write_Enable(not_1_out),
    .PC_out(pc4_1_pc_out));
  ROM #(.addrWidth(24), .dataWidth(32)) rom_1 (.addr(pc4_1_pc_out[23:0]), .data(rom_1_data));
  not not_1 (not_1_out, hazard_1_stall);
  IFID ifid_1 (
    .clk(clock_1_out), .PC_in(pc4_1_pc_out), .Write_Enable(not_1_out), .Instruction_In(rom_1_data),
    .PC_out(ifid_1_pc_out), .Instruction_Out(ifid_1_instruction_out), .Rs1(ifid_1_rs1), .Rs2(ifid_1_rs2),
    .Rd(ifid_1_rd));  // open: PC4_in, PC4_out
  Control_Unit control_unit_1 (
    .instruction(ifid_1_instruction_out), .Stall(hazard_1_stall), .Alu_Src(control_unit_1_alu_src),
    .Reg_Write(control_unit_1_reg_write), .Mem_To_Reg(control_unit_1_mem_to_reg),
    .Mem_Read(control_unit_1_mem_read), .Mem_Write(control_unit_1_mem_write), .Branch(control_unit_1_branch),
    .Soma_PC(control_unit_1_soma_pc), .Alu_Op(control_unit_1_alu_op), .S_funct7(control_unit_1_s_funct7),
    .S_funct3(control_unit_1_s_funct3), .S_opcode(control_unit_1_s_opcode),
    .Jump_Reg(control_unit_1_jump_reg), .mode(control_unit_1_mode), .Vector_size(control_unit_1_vector_size));
  RegisterFile registerfile_1 (
    .Read_Register_1(ifid_1_rs1), .Read_Register_2(ifid_1_rs2), .Write_Register(memwb_1_rd_out),
    .Write_Data(multiplexer_8_out), .Reg_Write(memwb_1_reg_write_out), .clk(clock_1_out),
    .Read_Data_1(registerfile_1_read_data_1), .Read_Data_2(registerfile_1_read_data_2));
  ImmGen immgen_1 (.instruction(ifid_1_instruction_out), .immediate(immgen_1_immediate));
  Hazard hazard_1 (
    .clk(clock_1_out), .Mem_Read_in(idex_1_mem_read_out), .Rd_EX(idex_1_rd_out), .Rs1(ifid_1_rs1),
    .Rs2(ifid_1_rs2), .stall(hazard_1_stall));
  IDEX idex_1 (
    .clk(clock_1_out), .ALU_Src_in(control_unit_1_alu_src), .ALU_Op_in(control_unit_1_alu_op),
    .funct3_in(control_unit_1_s_funct3), .funct7_in(control_unit_1_s_funct7), .PC_in(ifid_1_pc_out),
    .Soma_PC_in(control_unit_1_soma_pc), .Branch_in(control_unit_1_branch),
    .Mem_Write_in(control_unit_1_mem_write), .Mem_Read_in(control_unit_1_mem_read),
    .Reg_Write_in(control_unit_1_reg_write), .Mem_To_Reg_in(control_unit_1_mem_to_reg),
    .read1_in(registerfile_1_read_data_1), .read2_in(registerfile_1_read_data_2),
    .immediate_in(immgen_1_immediate), .Rd_in(ifid_1_rd), .Opcode_in(control_unit_1_s_opcode),
    .JumpReg_in(control_unit_1_jump_reg), .Rs1_In(ifid_1_rs1), .Rs2_In(ifid_1_rs1),
    .mode_in(control_unit_1_mode), .vector_size_in(control_unit_1_vector_size),
    .ALU_Src_out(idex_1_alu_src_out), .ALU_Op_out(idex_1_alu_op_out), .funct3_out(idex_1_funct3_out),
    .funct7_out(idex_1_funct7_out), .PC_out(idex_1_pc_out), .Soma_PC_out(idex_1_soma_pc_out),
    .Branch_out(idex_1_branch_out), .Mem_Write_out(idex_1_mem_write_out), .Mem_Read_out(idex_1_mem_read_out),
    .Reg_Write_out(idex_1_reg_write_out), .Mem_To_Reg_out(idex_1_mem_to_reg_out),
    .read1_out(idex_1_read1_out), .read2_out(idex_1_read2_out), .immediate_out(idex_1_immediate_out),
    .Rd_out(idex_1_rd_out), .Opcode_out(idex_1_opcode_out), .JumpReg_out(idex_1_jumpreg_out),
    .Rs1_out(idex_1_rs1_out), .Rs2_out(idex_1_rs2_out), .mode_out(idex_1_mode_out),
    .vector_size_out(idex_1_vector_size_out));
  not not_2 (not_2_out, idex_1_alu_src_out);
  Multiplexer #(.width(32)) multiplexer_2 (
    .in0(idex_1_read2_out), .in1(idex_1_immediate_out), .out(multiplexer_2_out), .sel(idex_1_alu_src_out));
  Multiplexer #(.width(32)) multiplexer_3 (
    .in0(idex_1_pc_out), .in1(idex_1_read1_out), .out(multiplexer_3_out), .sel(idex_1_jumpreg_out));
  Multiplexer #(.width(32)) multiplexer_4 (
    .in0(idex_1_read1_out), .in1(idex_1_pc_out), .out(multiplexer_4_out), .sel(idex_1_soma_pc_out));
  Multiplexer #(.width(32)) multiplexer_5 (
    .in0(multiplexer_2_out), .in1(32'h1), .out(multiplexer_5_out), .sel(and_1_out));
  and and_1 (and_1_out, not_2_out, idex_1_soma_pc_out);
  ALU_Control alu_control_1 (
    .Funct7(idex_1_funct7_out), .Funct3(idex_1_funct3_out), .Op_Code(idex_1_opcode_out),
    .Alu_Op(idex_1_alu_op_out), .ALU_Out(alu_control_1_alu_out), .Beq_Bne(alu_control_1_beq_bne));
  Multiplexer #(.select(2), .width(32)) multiplexer_6 (
    .in0(multiplexer_4_out), .in1(multiplexer_8_out),
    .in2({exmem_1_alu_result_out_2, exmem_1_alu_result_out}), .out(multiplexer_6_out));  // open: in3, sel
  Somador somador_1 (.A(multiplexer_3_out), .B(idex_1_immediate_out), .Z(somador_1_z));
  Multiplexer #(.select(2), .width(32)) multiplexer_7 (
    .in0(multiplexer_5_out), .in1(multiplexer_8_out),
    .in2({exmem_1_alu_result_out_2, exmem_1_alu_result_out}), .out(multiplexer_6_out));  // open: in3, sel
  ALU alu_1 (
    .A(multiplexer_6_out), .B(multiplexer_6_out), .controle(alu_control_1_alu_out), .mode(idex_1_mode_out),
    .vector_size(idex_1_vector_size_out), .result(alu_1_result), .f_zero(alu_1_f_zero));
  Forward forward_1 (
    .clk(clock_1_out), .reg_Write_WB(memwb_1_reg_write_out), .reg_Write_MEM(exmem_1_reg_write_out),
    .Rs1(idex_1_rs1_out), .Rs2(idex_1_rs2_out), .Rd_WB(memwb_1_rd_out), .Rd_Mem(exmem_1_rd_out),
    .forward_A(forward_1_forward_a), .forward_B(forward_1_forward_b));
  // AND_Gate and_2 has open pins: out=and_2_out
  EXMEM exmem_1 (
    .clk(clock_1_out), .Branch_in(idex_1_branch_out), .Mem_Write_in(idex_1_mem_write_out),
    .Mem_Read_in(idex_1_mem_read_out), .Reg_Write_in(idex_1_reg_write_out),
    .Mem_To_Reg_in(idex_1_mem_to_reg_out), .New_PC_in(somador_1_z), .Zero_in(and_2_out),
    .ALU_result_in(alu_1_result), .read2_in(idex_1_read2_out), .Rd_in(idex_1_rd_out),
    .Jalr_ou_Jal_in(and_1_out), .Branch_out(exmem_1_branch_out), .Mem_Write_out(exmem_1_mem_write_out),
    .Mem_Read_out(exmem_1_mem_read_out), .Reg_Write_out(exmem_1_reg_write_out),
    .Mem_To_Reg_out(exmem_1_mem_to_reg_out), .New_PC_out(exmem_1_new_pc_out), .Zero_out(exmem_1_zero_out),
    .ALU_result_out({exmem_1_alu_result_out_2, exmem_1_alu_result_out}), .read2_out(exmem_1_read2_out),
    .Rd_out(exmem_1_rd_out), .Jalr_ou_Jal_out(exmem_1_jalr_ou_jal_out));
  and and_3 (and_3_out, exmem_1_branch_out, exmem_1_zero_out);
  or or_1 (or_1_out, and_3_out, exmem_1_jalr_ou_jal_out);
  RAM #(.addrWidth(24), .dataWidth(32)) ram_1 (
    .addr(exmem_1_alu_result_out), .we(exmem_1_mem_read_out), .oe(exmem_1_mem_write_out), .clk(clock_1_out),
    .din(exmem_1_read2_out), .dout(ram_1_dout));
  MEMWB memwb_1 (
    .clk(clock_1_out), .Reg_Write_in(exmem_1_reg_write_out), .Mem_To_Reg_in(exmem_1_mem_to_reg_out),
    .Mem_data_in(ram_1_dout), .ALU_result_in({exmem_1_alu_result_out_2, exmem_1_alu_result_out}),
    .Rd_in(exmem_1_rd_out), .Reg_Write_out(memwb_1_reg_write_out), .Mem_To_Reg_out(memwb_1_mem_to_reg_out),
    .Mem_data_out(memwb_1_mem_data_out), .ALU_result_out(memwb_1_alu_result_out), .Rd_out(memwb_1_rd_out));
  Multiplexer #(.width(32)) multiplexer_8 (
    .in0(memwb_1_alu_result_out), .in1(memwb_1_mem_data_out), .out(multiplexer_8_out),
    .sel(memwb_1_mem_to_reg_out));
endmodule

// VHDL entity ALU, as the project stores it:
library IEEE;
use IEEE.STD_LOGIC_1164.ALL;
use ieee.numeric_std.ALL;
use IEEE.std_logic_unsigned.ALL;

entity ALU is
    port(
    A, B       : in std_logic_vector(31 downto 0);   -- Operandos A e B de 32 bits da ALU
    controle   : in std_logic_vector(3 downto 0);    -- Entrada responsável por determinar a operação da ALU
    result  : out std_logic_vector(31 downto 0);  -- Resultado da operação feita pela ALU
    f_zero     : out std_logic;                      -- Flag indicadora de resultado igual a zero na operacão da ALU
    mode       : in std_logic;                       -- Modo de operação: 0 para operação única e 1 para operação vetorial
    vector_size     : in std_logic_vector(1 downto 0)     -- Tamanho do vetor de operações (usado no modo vetorial)
    );
end ALU;


architecture Behavioral of ALU is

-- Declaração dos sinais temporários da ALU
signal result_nv : std_logic_vector(31 downto 0); -- Resultado não vetorial
signal result_v  : std_logic_vector(31 downto 0); -- Resultado vetorial
signal soma_v       : std_logic_vector(31 downto 0); -- Sinal temporário que armazena o resultado final da soma vetorial
signal sub_v        : std_logic_vector(31 downto 0); -- Sinal temporário que armazena o resultado final da subtração vetorial
signal shiftL_v     : std_logic_vector(31 downto 0); -- Sinal temporário que armazena o resultado final do Shift Left vetorial
signal shiftR_v     : std_logic_vector(31 downto 0); -- Sinal temporário que armazena o resultado final da Shift Right vetorial

signal A16_1 : std_logic_vector(15 downto 0);  -- Vetor que contém os bits de índice 31 até 16 do operando quando vecsize='10' (16 bits)
signal A16_2 : std_logic_vector(15 downto 0);  -- Vetor que contém os bits de índice 15 até 0 do operando quando vecsize='10' (16 bits)

signal A8_1 : std_logic_vector(7 downto 0);  -- Vetor que contém os bits de índice 31 até 24 do operando quando vecsize='01' (8 bits)
signal A8_2 : std_logic_vector(7 downto 0);  -- Vetor que contém os bits de índice 23 até 16 do operando quando vecsize='01' (8 bits)
signal A8_3 : std_logic_vector(7 downto 0);  -- Vetor que contém os bits de índice 15 até 8 do operando quando vecsize='01' (8 bits)
signal A8_4 : std_logic_vector(7 downto 0);  -- Vetor que contém os bits de índice 7 até 0 do operando quando vecsize='01' (8 bits)

signal A4_1 : std_logic_vector(3 downto 0);  -- Vetor que contém os bits de índice 31 até 28 do operando quando vecsize='00' (4 bits)
signal A4_2 : std_logic_vector(3 downto 0);  -- Vetor que contém os bits de índice 27 até 24 do operando quando vecsize='00' (4 bits)
signal A4_3 : std_logic_vector(3 downto 0);  -- Vetor que contém os bits de índice 23 até 20 do operando quando vecsize='00' (4 bits)
signal A4_4 : std_logic_vector(3 downto 0);  -- Vetor que contém os bits de índice 19 até 16 do operando quando vecsize='00' (4 bits)
signal A4_5 : std_logic_vector(3 downto 0);  -- Vetor que contém os bits de índice 15 até 12 do operando quando vecsize='00' (4 bits)
signal A4_6 : std_logic_vector(3 downto 0);  -- Vetor que contém os bits de índice 11 até 8 do operando quando vecsize='00' (4 bits)
signal A4_7 : std_logic_vector(3 downto 0);  -- Vetor que contém os bits de índice 7 até 4 do operando quando vecsize='00' (4 bits)
signal A4_8 : std_logic_vector(3 downto 0);  -- Vetor que contém os bits de índice 3 até 0 do operando quando vecsize='00' (4 bits)

signal integer_B : integer;                  -- Integer do valor binário que entra como operando B

begin

    -- Conversão da entrada B para integer para uso nas operações de deslocamento
    integer_B <= to_integer(unsigned(B));

    -- Divisão do sinal de entrada A em subvetores para as operações vetoriais
    A16_1 <= A(31 downto 16);
    A16_2 <= A(15 downto 0);

    A8_1 <= A(31 downto 24);
    A8_2 <= A(23 downto 16);
    A8_3 <= A(15 downto 8);
    A8_4 <= A(7 downto 0);

    A4_1 <= A(31 downto 28);
    A4_2 <= A(27 downto 24);
    A4_3 <= A(23 downto 20);
    A4_4 <= A(19 downto 16);
    A4_5 <= A(15 downto 12);
    A4_6 <= A(11 downto 8);
    A4_7 <= A(7 downto 4);
    A4_8 <= A(3 downto 0);
    
    
    -- Cálculos das operações vetoriais com base no tamanho do vetor (vecsize)
    soma_v <= (A + B) when vector_size = "11" else
             ((A16_1 + B(31 downto 16)) & (A16_2 + B(15 downto 0))) when vector_size = "10" else
             ((A8_1 + B(31 downto 24)) & (A8_2 + B(23 downto 16)) & (A8_3 + B(15 downto 8)) & (A8_4 + B(7 downto 0))) when vector_size = "01" else
             ((A4_1 + B(31 downto 28)) & (A4_2 + B(27 downto 24)) & (A4_3 + B(23 downto 20)) & (A4_4 + B(19 downto 16)) & (A4_5 + B(15 downto 12)) & (A4_6 + B(11 downto 8)) & (A4_7 + B(7 downto 4)) & (A4_8 + B(3 downto 0))) when vector_size = "00";
    
    sub_v <= (A - B) when vector_size = "11" else
             ((A16_1 - B(31 downto 16)) & (A16_2 - B(15 downto 0))) when vector_size = "10" else
             ((A8_1 - B(31 downto 24)) & (A8_2 - B(23 downto 16)) & (A8_3 - B(15 downto 8)) & (A8_4 - B(7 downto 0))) when vector_size = "01" else
             ((A4_1 - B(31 downto 28)) & (A4_2 - B(27 downto 24)) & (A4_3 - B(23 downto 20)) & (A4_4 - B(19 downto 16)) & (A4_5 - B(15 downto 12)) & (A4_6 - B(11 downto 8)) & (A4_7 - B(7 downto 4)) & (A4_8 - B(3 downto 0))) when vector_size = "00";
    
    -- Cálculos das operações de deslocamento vetoriais
    shiftL_v <= (std_logic_vector(shift_left(unsigned(A), integer_B))) when vector_size = "11" else
             ((std_logic_vector(shift_left(unsigned(A16_1), integer_B))) & std_logic_vector(shift_left(unsigned(A16_2), integer_B))) when vector_size = "10" else
             ((std_logic_vector(shift_left(unsigned(A8_1), integer_B))) & (std_logic_vector(shift_left(unsigned(A8_2), integer_B))) & (std_logic_vector(shift_left(unsigned(A8_3), integer_B))) & (std_logic_vector(shift_left(unsigned(A8_4), integer_B)))) when vector_size = "01" else
             ((std_logic_vector(shift_left(unsigned(A4_1), integer_B))) & (std_logic_vector(shift_left(unsigned(A4_2), integer_B))) & (std_logic_vector(shift_left(unsigned(A4_3), integer_B))) & (std_logic_vector(shift_left(unsigned(A4_4), integer_B))) & (std_logic_vector(shift_left(unsigned(A4_5), integer_B))) & (std_logic_vector(shift_left(unsigned(A4_6), integer_B))) & (std_logic_vector(shift_left(unsigned(A4_7), integer_B))) & (std_logic_vector(shift_left(unsigned(A4_8), integer_B)))) when vector_size = "00";

    shiftR_v <= (std_logic_vector(shift_right(unsigned(A), integer_B))) when vector_size = "11" else
             ((std_logic_vector(shift_right(unsigned(A16_1), integer_B))) & std_logic_vector(shift_right(unsigned(A16_2), integer_B))) when vector_size = "10" else
             ((std_logic_vector(shift_right(unsigned(A8_1), integer_B))) & (std_logic_vector(shift_right(unsigned(A8_2), integer_B))) & (std_logic_vector(shift_right(unsigned(A8_3), integer_B))) & (std_logic_vector(shift_right(unsigned(A8_4), integer_B)))) when vector_size = "01" else
             ((std_logic_vector(shift_right(unsigned(A4_1), integer_B))) & (std_logic_vector(shift_right(unsigned(A4_2), integer_B))) & (std_logic_vector(shift_right(unsigned(A4_3), integer_B))) & (std_logic_vector(shift_right(unsigned(A4_4), integer_B))) & (std_logic_vector(shift_right(unsigned(A4_5), integer_B))) & (std_logic_vector(shift_right(unsigned(A4_6), integer_B))) & (std_logic_vector(shift_right(unsigned(A4_7), integer_B))) & (std_logic_vector(shift_right(unsigned(A4_8), integer_B)))) when vector_size = "00";
    

    -- ALU vetorial (mode = 1) 
    result_v <= soma_v when controle = "0010" else
                sub_v when controle = "0110" else
                shiftL_v when controle = "0011" else
                shiftR_v when controle = "0111" else
                (others => '0');
    
    -- ALU não vetorial (mode = 0)
    result_nv <= (A + B) when controle = "0010" else
                   (A - B) when controle = "0110" else
                   (A XOR B) when controle = "0101" else
                   (A OR B) when controle = "0001" else
                   (A AND B) when controle = "0000" else
                   (std_logic_vector(shift_left(unsigned(A), integer_B))) when controle = "0011" else
                   (std_logic_vector(shift_right(unsigned(A), integer_B))) when controle = "0111";
    
    -- Seleção do resultado de acordo com o sinal de controle "mode"
    result <= result_nv when mode = '0' else
                result_v when mode = '1';
                
    -- Sinalização se o resultado é zero (serve para o Branch) -> como as operações vetoriais não incluem Branch, basta verificar do resultado não vetorial
    f_zero <= '1' when result_nv = "00000000000000000000000000000000" else '0';   

end Behavioral;

// VHDL entity ALU_Control, as the project stores it:
library IEEE;
use IEEE.STD_LOGIC_1164.ALL;

entity ALU_Control is
    port(
        Funct7    		: IN std_logic_vector(6 downto 0);    	 -- Entrada do funct7
        Funct3    		: IN std_logic_vector(2 downto 0);    	 -- Entrada do funct3
        Op_Code    		: IN std_logic_vector(6 downto 0);   	 -- Entrada do opcode
        Alu_Op   		: IN std_logic_vector(1 downto 0);       -- Entrada de códigos de operação da ALU (2 bits)
        ALU_Out	 	: OUT std_logic_vector(3 downto 0);      -- Saída do controle da ALU (4 bits)
        Beq_Bne		: OUT std_logic					 -- Sinal de controle para verificação de Beq ou Bne
        );
end ALU_Control;

architecture Behavioral of ALU_Control is
begin

	ALU_Out <= "0010" when Alu_Op = "00" else 	-- Operação de Load
			 	 "0110" when Alu_Op = "01" else 	-- Operação de Branch
			 	 "0010" when Funct7 = "0000000" and Funct3 = "000" else 	-- Operação de Soma
			 	 "0110" when Funct7 = "0100000" and Funct3 = "000" else 	-- Operação de Subtração
			 	 "0011" when Funct7 = "0000000" and Funct3 = "001" else 	-- Operação de Shift Left
			 	 "0101" when Funct7 = "0000000" and Funct3 = "100" else 	-- Operação XOR
			 	 "0111" when Funct7 = "0000000" and Funct3 = "101" else 	-- Operação de Shift Right
			 	 "0001" when Funct7 = "0000000" and Funct3 = "110" else 	-- Operação OR
			 	 "0000" when Funct7 = "0000000" and Funct3 = "111"; 		-- Operação AND
	Beq_Bne <= '1' when op_Code="1100011" and Funct3="000" else '0';			-- '1' quando a instrução for Beq
	 
end Behavioral;

// VHDL entity Control_Unit, as the project stores it:
library IEEE;
use IEEE.STD_LOGIC_1164.ALL;

entity Control_Unit is
    port(
        instruction                	: IN  std_logic_vector(31 downto 0);  -- Entrada da Instrução
        Stall                			: IN  std_logic;  				   -- Entrada do Hazard
        Alu_Src, Reg_Write, Mem_To_Reg 	: OUT std_logic;                      -- Sinais de Controle (1 Bit)
        Mem_Read, Mem_Write, Branch  	: OUT std_logic;                      -- Sinais de Controle (1 Bit)
        Soma_PC 					: OUT std_logic;			   	   -- Sinais de Controle (1 Bit)	
        Alu_Op		               	: OUT std_logic_vector(1 downto 0);   -- Saída da Operação da ALU (2 Bits)
        S_funct7 					: OUT std_logic_vector(6 downto 0);   -- Saída do Funct7
        S_funct3 					: OUT std_logic_vector(2 downto 0);   -- Saída do Funct3
        S_opcode 					: OUT std_logic_vector(6 downto 0);   -- Saída do Opcode
        Jump_Reg					: OUT std_logic;				   -- Indica quando a instrução é jalr	
        mode						: OUT std_logic;				   -- Indica se é uma operação vetorial
        Vector_size					: OUT std_logic_vector(1 downto 0));  -- Indica o tamanho do vetor
        
end Control_Unit;

architecture Behavioral of Control_Unit is

signal opcode : std_logic_vector(6 downto 0);	-- Opcode da Instrução
signal funct7 : std_logic_vector(6 downto 0);	-- Funct7 da Instrução
signal funct3 : std_logic_vector(2 downto 0);	-- Funct3 da Instrução


begin
	-- Definição do Opcode da Instrução
	opcode(0) <= instruction(0);
	opcode(1) <= instruction(1);
	opcode(2) <= instruction(2);
	opcode(3) <= instruction(3);
	opcode(4) <= instruction(4);
	opcode(5) <= instruction(5);
	opcode(6) <= instruction(6);
	Soma_PC <= '0'; 
	Jump_Reg <= '0';

	process(Stall)
	begin
		IF (Stall = '1') THEN
			Alu_Src <= '0';
			Reg_Write <= '0';
			Mem_To_Reg <= '0';
			Mem_Read <= '0';
			Mem_Write <= '0';
			Branch <= '0';
			Soma_PC <= '0';
			Jump_Reg <= '0';
		end if; 
	end process;
	-- Definição das Funct7, Funct3 e dos Sinais de Controle de acordo com o opcode.
	process(opcode)
	begin
		IF (opcode = "0110011") THEN		-- R-Type Instruction
			funct7(6) <= instruction(31);
			funct7(5) <= instruction(30);
			funct7(4) <= instruction(29);
			funct7(3) <= instruction(28);
			funct7(2) <= instruction(27);
			funct7(1) <= instruction(26);
			funct7(0) <= instruction(25);
			funct3(2) <= instruction (14);
			funct3(1) <= instruction (13);
			funct3(0) <= instruction (12);
			Alu_Src <= '0'; 			
			Reg_Write <= '1';
			Mem_To_Reg <= '0';
			Mem_Read <= '0';
			Mem_Write <= '0';
			Branch <= '0';
			mode <= '0';
			Vector_size <= "11";
			Alu_Op <= "10";
		END IF;
		IF (opcode = "0010011") THEN		-- I-Type Instruction (ADDi, ANDi, ORi, XORi, SLTi)
			funct7(6) <= '0';
			funct7(5) <= '0';
			funct7(4) <= '0';
			funct7(3) <= '0';
			funct7(2) <= '0';
			funct7(1) <= '0';
			funct7(0) <= '0';
			funct3(2) <= instruction (14);
			funct3(1) <= instruction (13);
			funct3(0) <= instruction (12);
			Alu_Src <= '1'; 			
			Reg_Write <= '1';
			Mem_To_Reg <= '0';
			Mem_Read <= '0';
			Mem_Write <= '0';
			Branch <= '0';
			mode <= '0';
			Vector_size <= "11";
			Alu_Op <= "10";
		END IF;
		IF (opcode = "0000011") THEN		-- I-Type Instruction (Load)
			funct7(6) <= '0';
			funct7(5) <= '0';
			funct7(4) <= '0';
			funct7(3) <= '0';
			funct7(2) <= '0';
			funct7(1) <= '0';
			funct7(0) <= '0';
			funct3(2) <= '0';
			funct3(1) <= '0';
			funct3(0) <= '0';
			Alu_Src <= '1'; 			
			Reg_Write <= '1';
			Mem_To_Reg <= '1';
			Mem_Read <= '1';
			Mem_Write <= '0';
			Branch <= '0';
			mode <= '0';
			Vector_size <= "11";
			Alu_Op <= "00";
		END IF;
		IF (opcode = "1100111") THEN		-- I-Type Instruction (Jump) 
			funct7(6) <= '0';
			funct7(5) <= '0';
			funct7(4) <= '0';
			funct7(3) <= '0';
			funct7(2) <= '0';
			funct7(1) <= '0';
			funct7(0) <= '0';
			funct3(2) <= '0';
			funct3(1) <= '0';
			funct3(0) <= '0';
			Alu_Src <= '0'; 			
			Reg_Write <= '0';
			Mem_To_Reg <= '0';
			Mem_Read <= '0';
			Mem_Write <= '0';
			Branch <= '0';
			Soma_PC <= '1';
			Jump_Reg <= '1';
			mode <= '0';
			Vector_size <= "11";
			Alu_Op <= "01";
		END IF;
		IF (opcode = "0100011") THEN		-- S-Type Instruction 
			funct7(6) <= '0';
			funct7(5) <= '0';
			funct7(4) <= '0';
			funct7(3) <= '0';
			funct7(2) <= '0';
			funct7(1) <= '0';
			funct7(0) <= '0';
			funct3(2) <= '0';
			funct3(1) <= '0';
			funct3(0) <= '0';
			Alu_Src <= '1'; 			
			Reg_Write <= '0';
			Mem_To_Reg <= '0';
			Mem_Read <= '0';
			Mem_Write <= '1';
			Branch <= '0';
			mode <= '0';
			Vector_size <= "11";
			Alu_Op <= "00";
		END IF;
		IF (opcode = "1101111") THEN		-- UJ-Type Instruction (jal)
			funct7(6) <= '0';
			funct7(5) <= '0';
			funct7(4) <= '0';
			funct7(3) <= '0';
			funct7(2) <= '0';
			funct7(1) <= '0';
			funct7(0) <= '0';
			funct3(2) <= '0';
			funct3(1) <= '0';
			funct3(0) <= '0';
			Alu_Src <= '0'; 			
			Reg_Write <= '1';
			Mem_To_Reg <= '0';
			Mem_Read <= '0';
			Mem_Write <= '0';
			Branch <= '0';
			Soma_PC <= '1';
			mode <= '0';
			Vector_size <= "11";
			Alu_Op <= "10";
		END IF;
		IF (opcode = "0110111") THEN		-- U-Type Instruction (lui - soma com imediato muito grande)
			funct7(6) <= '0';
			funct7(5) <= '0';
			funct7(4) <= '0';
			funct7(3) <= '0';
			funct7(2) <= '0';
			funct7(1) <= '0';
			funct7(0) <= '0';
			funct3(2) <= '0';
			funct3(1) <= '0';
			funct3(0) <= '0';
			Alu_Src <= '1'; 			
			Reg_Write <= '1';
			Mem_To_Reg <= '0';
			Mem_Read <= '0';
			Mem_Write <= '0';
			Branch <= '0';
			mode <= '0';
			Vector_size <= "11";
			Alu_Op <= "10";
		END IF;
		IF (opcode = "0010111") THEN		-- U-Type Instruction (auipc, soma do pc com o imediato e guarda no registrador)
			funct7(6) <= '0';
			funct7(5) <= '0';
			funct7(4) <= '0';
			funct7(3) <= '0';
			funct7(2) <= '0';
			funct7(1) <= '0';
			funct7(0) <= '0';
			funct3(2) <= '0';
			funct3(1) <= '0';
			funct3(0) <= '0';
			Alu_Src <= '1'; 			
			Reg_Write <= '1';
			Mem_To_Reg <= '0';
			Mem_Read <= '0';
			Mem_Write <= '0';
			Branch <= '0';
			Soma_PC <= '1';
			mode <= '0';
			Vector_size <= "11";
			Alu_Op <= "10";
		END IF;
		IF (opcode = "1100011") THEN		-- Sb-Type Instruction 
			funct7(6) <= '0';
			funct7(5) <= '0';
			funct7(4) <= '0';
			funct7(3) <= '0';
			funct7(2) <= '0';
			funct7(1) <= '0';
			funct7(0) <= '0';
			funct3(2) <= instruction (14);
			funct3(1) <= instruction (13);
			funct3(0) <= instruction (12);
			Alu_Src <= '0'; 			
			Reg_Write <= '0';
			Mem_To_Reg <= '0';
			Mem_Read <= '0';
			Mem_Write <= '0';
			Branch <= '1';
			mode <= '0';
			Vector_size <= "11";
			Alu_Op <= "01";
		END IF;
		IF (opcode = "1111100") 	THEN		-- R-Type Vetorial Instruction (4bits)
			funct7(6) <= instruction(31);
			funct7(5) <= instruction(30);
			funct7(4) <= instruction(29);
			funct7(3) <= instruction(28);
			funct7(2) <= instruction(27);
			funct7(1) <= instruction(26);
			funct7(0) <= instruction(25);
			funct3(2) <= instruction (14);
			funct3(1) <= instruction (13);
			funct3(0) <= instruction (12);
			Alu_Src <= '0'; 			
			Reg_Write <= '1';
			Mem_To_Reg <= '0';
			Mem_Read <= '0';
			Mem_Write <= '0';
			Branch <= '0';
			mode <= '1';
			Vector_size <= "00";
			Alu_Op <= "10";
		END IF;
		IF (opcode = "1111101")  THEN				-- R-Type Vetorial Instruction (8bits)
			funct7(6) <= instruction(31);
			funct7(5) <= instruction(30);
			funct7(4) <= instruction(29);
			funct7(3) <= instruction(28);
			funct7(2) <= instruction(27);
			funct7(1) <= instruction(26);
			funct7(0) <= instruction(25);
			funct3(2) <= instruction (14);
			funct3(1) <= instruction (13);
			funct3(0) <= instruction (12);
			Alu_Src <= '0'; 			
			Reg_Write <= '1';
			Mem_To_Reg <= '0';
			Mem_Read <= '0';
			Mem_Write <= '0';
			Branch <= '0';
			mode <= '1';
			Vector_size <= "01";
			Alu_Op <= "10";
		END IF;
		IF (opcode = "1111110")	THEN			-- R-Type Vetorial Instruction (16bits)
			funct7(6) <= instruction(31);
			funct7(5) <= instruction(30);
			funct7(4) <= instruction(29);
			funct7(3) <= instruction(28);
			funct7(2) <= instruction(27);
			funct7(1) <= instruction(26);
			funct7(0) <= instruction(25);
			funct3(2) <= instruction (14);
			funct3(1) <= instruction (13);
			funct3(0) <= instruction (12);
			Alu_Src <= '0'; 			
			Reg_Write <= '1';
			Mem_To_Reg <= '0';
			Mem_Read <= '0';
			Mem_Write <= '0';
			Branch <= '0';
			mode <= '1';
			Vector_size <= "10";
			Alu_Op <= "10";
		END IF;
		IF (opcode = "1111000") THEN		-- I-Type Vetorial Instruction (Soma e deslocamento)(4bits)
			funct7(6) <= '0';
			funct7(5) <= '0';
			funct7(4) <= '0';
			funct7(3) <= '0';
			funct7(2) <= '0';
			funct7(1) <= '0';
			funct7(0) <= '0';
			funct3(2) <= instruction (14);
			funct3(1) <= instruction (13);
			funct3(0) <= instruction (12);
			Alu_Src <= '1'; 			
			Reg_Write <= '1';
			Mem_To_Reg <= '0';
			Mem_Read <= '0';
			Mem_Write <= '0';
			Branch <= '0';
			mode <= '1';
			Vector_size <= "00";
			Alu_Op <= "10";
		END IF;
		IF (opcode = "1111001") THEN		-- I-Type Vetorial Instruction (Soma e deslocamento)(8bits)
			funct7(6) <= '0';
			funct7(5) <= '0';
			funct7(4) <= '0';
			funct7(3) <= '0';
			funct7(2) <= '0';
			funct7(1) <= '0';
			funct7(0) <= '0';
			funct3(2) <= instruction (14);
			funct3(1) <= instruction (13);
			funct3(0) <= instruction (12);
			Alu_Src <= '1'; 			
			Reg_Write <= '1';
			Mem_To_Reg <= '0';
			Mem_Read <= '0';
			Mem_Write <= '0';
			Branch <= '0';
			mode <= '1';
			Vector_size <= "01";
			Alu_Op <= "10";
		END IF;
		IF (opcode = "1111010") THEN		-- I-Type Vetorial Instruction (Soma e deslocamento)(16bits)
			funct7(6) <= '0';
			funct7(5) <= '0';
			funct7(4) <= '0';
			funct7(3) <= '0';
			funct7(2) <= '0';
			funct7(1) <= '0';
			funct7(0) <= '0';
			funct3(2) <= instruction (14);
			funct3(1) <= instruction (13);
			funct3(0) <= instruction (12);
			Alu_Src <= '1'; 			
			Reg_Write <= '1';
			Mem_To_Reg <= '0';
			Mem_Read <= '0';
			Mem_Write <= '0';
			Branch <= '0';
			mode <= '1';
			Vector_size <= "10";
			Alu_Op <= "10";
		END IF;
		IF (opcode = "1110000") THEN		-- U-Type Vetorial Instruction (4bits)(auipc)
			funct7(6) <= '0';
			funct7(5) <= '0';
			funct7(4) <= '0';
			funct7(3) <= '0';
			funct7(2) <= '0';
			funct7(1) <= '0';
			funct7(0) <= '0';
			funct3(2) <= '0';
			funct3(1) <= '0';
			funct3(0) <= '0';
			Alu_Src <= '1'; 			
			Reg_Write <= '1';
			Mem_To_Reg <= '0';
			Mem_Read <= '0';
			Mem_Write <= '0';
			Branch <= '0';
			Soma_PC <= '1';
			mode <= '1';
			Vector_size <= "00";
			Alu_Op <= "10";
		END IF;
		IF (opcode = "1110001") THEN		-- U-Type Vetorial Instruction (4bits)(auipc)
			funct7(6) <= '0';
			funct7(5) <= '0';
			funct7(4) <= '0';
			funct7(3) <= '0';
			funct7(2) <= '0';
			funct7(1) <= '0';
			funct7(0) <= '0';
			funct3(2) <= '0';
			funct3(1) <= '0';
			funct3(0) <= '0';
			Alu_Src <= '1'; 			
			Reg_Write <= '1';
			Mem_To_Reg <= '0';
			Mem_Read <= '0';
			Mem_Write <= '0';
			Branch <= '0';
			Soma_PC <= '1';
			mode <= '1';
			Vector_size <= "01";
			Alu_Op <= "10";
		END IF;
		IF (opcode = "1110010") THEN		-- U-Type Vetorial Instruction (4bits)(auipc)
			funct7(6) <= '0';
			funct7(5) <= '0';
			funct7(4) <= '0';
			funct7(3) <= '0';
			funct7(2) <= '0';
			funct7(1) <= '0';
			funct7(0) <= '0';
			funct3(2) <= '0';
			funct3(1) <= '0';
			funct3(0) <= '0';
			Alu_Src <= '1'; 			
			Reg_Write <= '1';
			Mem_To_Reg <= '0';
			Mem_Read <= '0';
			Mem_Write <= '0';
			Branch <= '0';
			Soma_PC <= '1';
			mode <= '1';
			Vector_size <= "10";
			Alu_Op <= "10";
		END IF;
	end process;
	S_funct7 <= funct7;
	S_funct3 <= funct3;
	S_opcode <= opcode;
end Behavioral;

// VHDL entity ImmGen, as the project stores it:
library IEEE;
use IEEE.STD_LOGIC_1164.ALL;
USE IEEE.NUMERIC_STD.ALL;

entity ImmGen is
    Port( 
        instruction: in std_logic_vector(31 downto 0);  	-- Entrada da Instrução 
        immediate: out std_logic_vector(31 downto 0)  		-- Saída do Valor Imediato
        );
end ImmGen;

architecture Behavioral of ImmGen is
    signal opcode       : std_logic_vector(6 downto 0);  		-- Sinal para armazenr o opcode da instrução
    signal S_imm  : std_logic_vector(31 downto 0) := "00000000000000000000000000000000";  -- Sinal auxiliar para definição do imediato

begin

    opcode <= instruction(6 downto 0);  -- Definição do opcode

    process(opcode)
    begin
        if (opcode = "0010011" or opcode = "0000011" or opcode = "1100111") then  	-- Tipo I 
            S_imm(11 downto 0)  <= instruction(31 downto 20);  					-- Seleciona o imediato 
            S_imm(31 downto 12) <= (others => instruction(31));  				-- Extensão do Bit de Sinal
        elsif (opcode = "1101111") then  									-- Tipo UJ 
            S_imm(20) <= instruction(31);  									-- Seleciona o imediato
            S_imm(10 downto 1) <= instruction(30 downto 21);					-- Seleciona o imediato
            S_imm(11) <= instruction(20);									-- Seleciona o imediato	
            S_imm(19 downto 12) <= instruction(19 downto 12);					-- Seleciona o imediato
            S_imm(31 downto 21) <= (others => instruction(31));					-- Extensão do Bit de Sinal
        elsif (opcode = "0110111" or opcode = "0010111") then										-- Tipo U 
        	  S_imm(31 downto 12) <= instruction(31 downto 12);  					-- Seleciona o imediato	
        elsif (opcode = "0100011") then  									-- Tipo S 
            S_imm(11 downto 5)  <= instruction(31 downto 25);  					-- Seleciona o imediato
            S_imm(4 downto 0)   <= instruction(11 downto 7);   					-- Seleciona o imediato
            S_imm(31 downto 12) <= (others => instruction(31));  				-- Extensão do Bit de Sinal
        elsif (opcode = "1100011") then  									-- Tipo SB
            S_imm(12)           <= instruction(31);          					-- Seleciona o imediato
            S_imm(11)           <= instruction(7);           					-- Seleciona o imediato
            S_imm(10 downto 5)  <= instruction(30 downto 25);  					-- Seleciona o imediato
            S_imm(4 downto 1)   <= instruction(11 downto 8);   					-- Seleciona o imediato
            S_imm(31 downto 13) <= (others => instruction(31));  				-- Extensão do Bit de Sinal
        end if;
    end process;

    immediate <= S_imm;  												-- Atribui o valor imeadiato à saída

end Behavioral;

// VHDL entity PC4, as the project stores it:
library IEEE;
use IEEE.STD_LOGIC_1164.ALL;
use ieee.numeric_std.ALL;
use IEEE.std_logic_unsigned.ALL;


ENTITY PC4 IS
  PORT (
    clk      : IN  std_logic;                    		-- Entrada do Clock
    reset    : IN  std_logic;                    		-- Entrada de Reset
    PC_in    : IN  std_logic_vector(31 DOWNTO 0); 	-- Entrada do endereço atual
    Write_Enable   : IN std_logic;               		-- Entrada de Habilitação de escrita no PC
    PC_out   : OUT std_logic_vector(31 DOWNTO 0)  	-- Saída do próximo endereço
    );
END PC4;

ARCHITECTURE Behavioral OF PC4 IS

BEGIN

	PROCESS (clk, reset, Write_Enable)
	BEGIN
		IF (rising_edge(clk)) THEN                      				-- Detecção do Clock
			if (PC_in = "UUUUUUUUUUUUUUUUUUUUUUUUUUUUUUUU") then   	-- Verificação de endereço indefinido
				PC_out <= (others => '0');               			-- Caso indefinido, início no primeiro endereço
			elsif (Write_Enable = '0') then              				-- WriteEnable desabilitado
				PC_out <= PC_in;								-- Manutenção do endereço atual
			elsif (Write_Enable = '1') then						-- WriteEnable habilitado
				PC_out <= PC_in + '1';							-- Atualização do endereço
			end if;
		END IF;
		IF (reset = '1') THEN                           				-- Detecção de Reset
			PC_out <= (others => '0');                   			-- Retorno ao primeiro endereço
		END IF;
	END PROCESS;

END Behavioral;

// VHDL entity Somador, as the project stores it:
LIBRARY ieee;
USE ieee.std_logic_1164.all;
USE IEEE.std_logic_unsigned.ALL; 

ENTITY Somador IS
  PORT (
    A, B        : IN  std_logic_vector(31 DOWNTO 0); 	-- Entrada de vetores de 32 bits
    Z           : OUT std_logic_vector(31 DOWNTO 0) 	-- Saída do vetor resultado da soma
    );
END Somador;

ARCHITECTURE Behavioral OF somador IS

BEGIN

Z <= A + B; 									-- Vetor resultado da soma

END Behavioral;

// VHDL entity RegisterFile, as the project stores it:
library ieee;
use ieee.std_logic_1164.all;
use ieee.numeric_std.all;

entity RegisterFile is
  port(
    Read_Register_1           : in std_logic_vector(4 downto 0);    	-- Endereço do primeiro registrador a ser lido
    Read_Register_2           : in std_logic_vector(4 downto 0);    	-- Endereço do segundo registrador a ser lido
    Write_Register      	    : in std_logic_vector(4 downto 0);    	-- Endereço do registrador a ser escrito
    Write_Data                : in  std_logic_vector(31 downto 0);     -- Dado a ser escrito
    Reg_Write  			    : in  std_logic;     				-- Sinal de controle
    Read_Data_1         	    : out  std_logic_vector(31 downto 0);    -- Dado do primeiro registrador lido
    Read_Data_2       	    : out  std_logic_vector(31 downto 0);    -- Dado do segundo registrador lido
    clk                 	    : in  std_logic                        	-- Sinal do CLOCK
    );
end RegisterFile;

architecture Behavioral of RegisterFile is
  type RegisterFile is array(0 to 31) of std_logic_vector(31 downto 0);
  signal Registers : RegisterFile := 
   ("00000000000000000000000000000000","00000000000000000000000000000000","00000000000000000000000000000000","00000000000000000000000000000000",
    "00000000000000000000000000000000","00000000000000000000000000000000","00000000000000000000000000000000","00000000000000000000000000000000",
    "00000000000000000000000000000000","00000000000000000000000000000000","00000000000000000000000000000000","00000000000000000000000000000000",
    "00000000000000000000000000000000","00000000000000000000000000000000","00000000000000000000000000000000","00000000000000000000000000000000",
    "00000000000000000000000000000000","00000000000000000000000000000000","00000000000000000000000000000000","00000000000000000000000000000000",
    "00000000000000000000000000000000","00000000000000000000000000000000","00000000000000000000000000000000","00000000000000000000000000000000",
    "00000000000000000000000000000000","00000000000000000000000000000000","00000000000000000000000000000000","00000000000000000000000000000000",
    "00000000000000000000000000000000","00000000000000000000000000000000","00000000000000000000000000000000","00000000000000000000000000000000");

begin
  regFile : process (clk) is
  begin
    if falling_edge(clk) then
      if (Registers(to_integer(unsigned(Read_Register_1))) = "UUUUUUUUUUUUUUUUUUUUUUUUUUUUUUUU") THEN -- Caso o valor do registrador esteja indefinido, a saída será "000..."
      	Read_Data_1 <= (others => '0');  
      ELSE 
      	Read_Data_1 <= registers(to_integer(unsigned(Read_Register_1)));  -- Leitura do valor contido no registrador 1
      END IF;
      IF (Registers(to_integer(unsigned(Read_Register_2))) = "UUUUUUUUUUUUUUUUUUUUUUUUUUUUUUUU") THEN -- Caso o valor do registrador esteja indefinido, a saída será "000..."
      	Read_Data_2 <= (others => '0');  
      ELSE
      	Read_Data_2 <= registers(to_integer(unsigned(Read_Register_2)));  -- Leitura do valor contido no registrador 2 
      END IF;
    end if; 
    if rising_edge(clk) then
      if Reg_Write = '1' then
        Registers(to_integer(unsigned(Write_Register))) <= Write_Data;      -- Escrita do valor no registrador selecionado
      end if;
    end if;
  end process;
  
end Behavioral;

// VHDL entity IFID, as the project stores it:
LIBRARY ieee;
USE ieee.std_logic_1164.all;

ENTITY IFID IS
  PORT (
    clk         : IN  std_logic;                    -- Entrada do CLOCK
    PC_in        : IN  std_logic_vector(31 DOWNTO 0); -- Entrada do valor atual do PC (contador de programa)
    PC4_in	 : IN  std_logic_vector(31 downto 0); -- Entrada do valor do PC mais 4 (próxima instrução)
    Write_Enable   : IN std_logic;                 -- Entrada do sinal de habilitação de escrita no IFID
    Instruction_In      : IN  std_logic_vector(31 DOWNTO 0); -- Entrada da instrução atual buscada na memória de instruções
    PC_out       : OUT std_logic_vector(31 DOWNTO 0); -- Saída do valor atual do PC (contador de programa)
    PC4_out	 : OUT std_logic_vector(31 downto 0); -- Saída do valor do PC mais 4 (próxima instrução)
    Instruction_Out     : OUT std_logic_vector(31 DOWNTO 0);  -- Saída da instrução atual buscada na memória de instruções
    Rs1 : OUT std_logic_vector(4 DOWNTO 0);  -- Saída da instrução atual buscada na memória de instruções
    Rs2 : OUT std_logic_vector(4 DOWNTO 0);  -- Saída da instrução atual buscada na memória de instruções
    Rd : OUT std_logic_vector(4 DOWNTO 0)  -- Saída da instrução atual buscada na memória de instruções
    );
END IFID;


ARCHITECTURE Behavioral OF IFID IS

signal opcode : std_logic_vector(6 downto 0);	-- Opcode da Instrução
signal s_Rs1 : std_logic_vector(4 downto 0);		-- Rs1 da Instrução
signal s_Rs2 : std_logic_vector(4 downto 0);		-- Rs2 da Instrução
signal s_Rd : std_logic_vector(4 downto 0);		-- Rd da Instrução
SIGNAL IDIF : std_logic_vector(117 DOWNTO 0);  	-- Registrador de 96 bits para armazenar os valores do IFID

BEGIN
	-- Definição do Opcode da Instrução
	opcode(0) <= Instruction_In(0);
	opcode(1) <= Instruction_In(1);
	opcode(2) <= Instruction_In(2);
	opcode(3) <= Instruction_In(3);
	opcode(4) <= Instruction_In(4);
	opcode(5) <= Instruction_In(5);
	opcode(6) <= Instruction_In(6);

	process(opcode)
	begin
	-- Rs1
		IF NOT (opcode = "1101111" or opcode = "0110111") THEN  -- Tipos diferentes de U e UJ tem Rs1
		s_Rs1 (0) <= Instruction_In(15);
		s_Rs1 (1) <= Instruction_In(16);
		s_Rs1 (2) <= Instruction_In(17);
		s_Rs1 (3) <= Instruction_In(18);
		s_Rs1 (4) <= Instruction_In(19);
		END IF;

	-- Rs2
		IF (opcode = "0110011" or opcode = "0100011" or opcode = "1100011") THEN  -- Tipos R, S e Sb tem Rs2
		s_Rs2 (0) <= Instruction_In(20);
		s_Rs2 (1) <= Instruction_In(21);
		s_Rs2 (2) <= Instruction_In(22);
		s_Rs2 (3) <= Instruction_In(23);
		s_Rs2 (4) <= Instruction_In(24);
		END IF;

	-- Rd
		IF NOT (opcode = "0100011" or opcode = "1100011") THEN  -- Tipos diferentes de S e Sb tem Rd
		s_Rd (0) <= Instruction_In(7); 
		s_Rd (1) <= Instruction_In(8);
		s_Rd (2) <= Instruction_In(9);
		s_Rd (3) <= Instruction_In(10);
		s_Rd (4) <= Instruction_In(11);
		END IF;
	end process;

	
	PROCESS (clk, Write_Enable)
	BEGIN
		IF (rising_edge(clk)) THEN                   	-- Detecção de subida de CLOCK
			if (Write_Enable = '1') then             	-- Vericação se o WriteEnable está habilitado
				IDIF(31 DOWNTO 0) <= Instruction_In;       
				IDIF(63 DOWNTO 32) <= PC_in;          	-- Armazena o valor atual do PC
				IDIF(95 downto 64) <= PC4_in;       	-- Armazena o valor do PC mais 4 (próxima instrução)
				IDIF(102 downto 96) <= opcode;		-- Armazena o opcode
				IDIF(107 downto 103) <= s_Rs1;		-- Armazena o Rs1
				IDIF(112 downto 108) <= s_Rs2;		-- Armazena o Rs2
				IDIF(117 downto 113) <= s_Rd;			-- Armazena o Rd
			end if;
		END IF;
		IF (falling_edge(clk)) THEN                 		-- Detecção de descida de CLOCK
			PC_out <= IDIF(63 DOWNTO 32);           	-- Definição do PC atual
			Instruction_Out <= IDIF(31 DOWNTO 0);        -- Definição da instrução armazenada
			PC4_out <= IDIF(95 downto 64);        		-- Saída de PC+4
			Rs1 <= IDIF(107 downto 103);				-- Saída do Rs1
			Rs2 <= IDIF(112 downto 108);				-- Saída do Rs2
			Rd <= IDIF(117 downto 113);				-- Saída do Rd
		END IF;
	END PROCESS;
	
END Behavioral;

// VHDL entity IDEX, as the project stores it:
LIBRARY ieee;
USE ieee.std_logic_1164.all;

ENTITY IDEX IS
  PORT (
    clk             : IN std_logic;                             -- Entrada do sinal de clock            
    ALU_Src_in       : IN std_logic;                             -- Entradas do ALUSrc e ALUOp, que são sinais de controle para a ALU_Control
    ALU_Op_in        : IN std_logic_vector(1 downto 0);          -- ALUSrc e ALUOp são usados no estágio EX do pipeline, então não aparecem nos proximos regs do pipeline
    funct3_in       : IN std_logic_vector(2 downto 0);          -- Entrada do Funct3, usado na ALU_Control
    funct7_in       : IN std_logic_vector(6 downto 0);          -- Entrada do Funct7, usado na ALU_Control
    PC_in           : IN std_logic_vector(31 DOWNTO 0);         -- Entrada do valor atual do PC (contador de programa)
    Soma_PC_in      : IN std_logic;                             -- Entrada do sinal de controle que define quando o PC deve ser somado (jal)        
    Branch_in       : IN std_logic;                             -- Entrada do sinal de controle que define quando ocorre Branch
    Mem_Write_in     : IN std_logic;                             -- Entrada do sinal de controle que define quando a Memória será escrita
    Mem_Read_in      : IN std_logic;                             -- Entrada do sinal de controle que define quando a Memória será lida
    Reg_Write_in     : IN std_logic;                             -- Entrada do sinal de controle que define quando o registrador será escrito
    Mem_To_Reg_in     : IN std_logic;                             -- Entrada do sinal de controle que define quando um dado será passado da memória para o registrador
    read1_in        : IN std_logic_vector(31 DOWNTO 0);         -- Entrada do valor lido do read data 1
    read2_in        : IN std_logic_vector(31 DOWNTO 0);         -- Entrada do valor lido do read data 2
    immediate_in    : in std_logic_vector(31 DOWNTO 0);         -- Entrada do imediato gerado pelo ImmGen
    Rd_in           : IN std_logic_vector(4 DOWNTO 0);          -- Entrada da instrução atual buscada na memória de instruções
    Opcode_in       : IN std_logic_vector(6 DOWNTO 0);          -- Entrada do Opcode
    JumpReg_in      : IN std_Logic;                             -- Entrada do JumpReg
    Rs1_In          : IN std_logic_vector(4 downto 0);          -- Entrada do Rs1   
    Rs2_In          : IN std_logic_vector(4 downto 0);          -- Entrada do Rs2
    mode_in         : in std_logic;                             -- Modo de operação: 0 para operação única e 1 para operação vetorial
    vector_size_in      : in std_logic_vector(1 downto 0);          -- Tamanho do vetor de operações (usado no modo vetorial)
  
    ALU_Src_out      : out std_logic;                            -- Saídas do ALUSrc e ALUOp, que são sinais de controle para a ALU_Control
    ALU_Op_out       : out std_logic_vector(1 downto 0);         -- ALUSrc e ALUOp são usados no estágio EX do pipeline, então não aparecem nos proximos regs do pipeline
    funct3_out      : out std_logic_vector(2 downto 0);         -- Saída do Funct3, usado na ALU_Control    
    funct7_out      : out std_logic_vector(6 downto 0);         -- Saída do Funct7, usado na ALU_Control
    PC_out          : out std_logic_vector(31 DOWNTO 0);        -- Saída do valor atual do PC (contador de programa)
    Soma_PC_out     : out std_logic;                            -- Saída do sinal de controle que define quando o PC deve ser somado (jal)
    Branch_out      : out std_logic;                            -- Saída do sinal de controle que define quando ocorre Branch
    Mem_Write_out    : out std_logic;                            -- Saída do sinal de controle que define quando a Memória será escrita
    Mem_Read_out     : out std_logic;                            -- Saída do sinal de controle que define quando a Memória será lida
    Reg_Write_out    : out std_logic;                            -- Saída do sinal de controle que define quando o registrador será escrito
    Mem_To_Reg_out    : out std_logic;                            -- Saída do sinal de controle que define quando um dado será passado da memória para o registrador
    read1_out       : out std_logic_vector(31 DOWNTO 0);        -- Saída do valor lido do read data 1
    read2_out       : out std_logic_vector(31 DOWNTO 0);        -- Saída do valor lido do read data 2   
    immediate_out   : out std_logic_vector(31 DOWNTO 0);        -- Saída do imediato gerado pelo ImmGen
    Rd_out          : out std_logic_vector(4 DOWNTO 0);         -- Saída da instrução atual buscada na memória de instruções
    Opcode_out      : out std_logic_vector(6 DOWNTO 0);         -- Saída do Opcode
    JumpReg_out     : out std_Logic;                            -- Saída do JumpReg
    Rs1_out         : out std_logic_vector(4 downto 0);         -- Saída do Rs1 
    Rs2_out         : out std_logic_vector(4 downto 0);          -- Saída do Rs2
    mode_out        : out std_logic;                            -- Modo de operação: 0 para operação única e 1 para operação vetorial
    vector_size_out     : out std_logic_vector(1 downto 0)          -- Tamanho do vetor de operações (usado no modo vetorial)
    );  
END IDEX;


ARCHITECTURE Behavioral OF IDEX IS

SIGNAL idex_sig : std_logic_vector(173 DOWNTO 0);  -- Registrador de 151 bits para armazenar os valores do IDEX

BEGIN

    PROCESS (clk)
    BEGIN
        IF (rising_edge(clk)) THEN                   -- Detecção de subida de CLOCK
            idex_sig(0) <= ALU_Src_in;          
            idex_sig(2 downto 1) <= ALU_Op_in;          
            idex_sig(5 DOWNTO 3) <= funct3_in;      
            idex_sig(12 DOWNTO 6) <= funct7_in;
            idex_sig(44 DOWNTO 13) <= PC_in ;  
            idex_sig(45) <= Soma_PC_in;       
            idex_sig(46) <= Branch_in;   
            idex_sig(47) <= Mem_Write_in;   
            idex_sig(48) <= Mem_Read_in;   
            idex_sig(49) <= Reg_Write_in;   
            idex_sig(50) <= Mem_To_Reg_in;   
            idex_sig(82 DOWNTO 51) <= read1_in;    
            idex_sig(114 DOWNTO 83) <= read2_in;    
            idex_sig(146 DOWNTO 115) <= immediate_in;   
            idex_sig(152 DOWNTO 147) <= Rd_in;
            idex_sig(159 downto 153) <= Opcode_in; 
            idex_sig(160) <= JumpReg_in;  
            idex_sig(165 downto 161) <= Rs1_In;
            idex_sig(170 downto 166) <= Rs2_In;
            idex_sig(171) <= mode_in;        
            idex_sig(173 downto 172) <= vector_size_in;   
        END IF;
        IF (falling_edge(clk)) THEN                 -- Detecção de descida de CLOCK
            ALU_Src_out <= idex_sig(0);       
            ALU_Op_out  <= idex_sig(2 downto 1);     
            funct3_out <= idex_sig(5 DOWNTO 3);      
            funct7_out <= idex_sig(12 DOWNTO 6);    
            PC_out <= idex_sig(44 DOWNTO 13);
            Soma_PC_out <= idex_sig(45);
            Branch_out <= idex_sig(46);
            Mem_Write_out <= idex_sig(47);
            Mem_Read_out <= idex_sig(48);
            Reg_Write_out <= idex_sig(49);
            Mem_To_Reg_out <= idex_sig(50);
            read1_out <= idex_sig(82 DOWNTO 51);
            read2_out <= idex_sig(114 DOWNTO 83);
            immediate_out <= idex_sig(146 DOWNTO 115);
            Rd_out <= idex_sig(152 DOWNTO 147);
            Opcode_out <= idex_sig(159 downto 153);
            JumpReg_out <= idex_sig(160);
            Rs1_out <= idex_sig(165 downto 161);
            Rs2_out <= idex_sig(170 downto 166);
            mode_out <= idex_sig(171);
            vector_size_out <= idex_sig(173 downto 172);
            
        END IF;
    END PROCESS;

    
END Behavioral;

// VHDL entity EXMEM, as the project stores it:
LIBRARY ieee;
USE ieee.std_logic_1164.all;

ENTITY EXMEM IS
  PORT (
    clk             : IN std_logic;                             -- Entrada do sinal de clock            
    Branch_in       : IN std_logic;                             -- Entrada do sinal de controle que define quando ocorre Branch
    Mem_Write_in     : IN std_logic;                             -- Entrada do sinal de controle que define quando a Memória será escrita
    Mem_Read_in      : IN std_logic;                             -- Entrada do sinal de controle que define quando a Memória será lida
    Reg_Write_in     : IN std_logic;                             -- Entrada do sinal de controle que define quando o registrador será escrito
    Mem_To_Reg_in     : IN std_logic;                             -- Entrada do sinal de controle que define quando um dado será passado da memória para o registrador
    New_PC_in       : IN std_logic_vector(31 DOWNTO 0);         -- Soma do PC com imediato (jal) ou reg com imediato substituindo PC (jalr)
    Zero_in         : IN std_logic;                             -- Quando o resultado da ALU foi zero (serve para Branch)
    ALU_result_in    : IN std_logic_vector(31 DOWNTO 0);         -- Entrada do resultado da operação da ALU
    read2_in        : IN std_logic_vector(31 DOWNTO 0);         -- Entrada do valor lido do read data 2
    Rd_in           : IN std_logic_vector(4 DOWNTO 0);          -- Entrada da instrução atual buscada na memória de instruções
    Jalr_ou_Jal_in	: IN std_logic;					    -- Entrada que indica se é Jalr ou Jal	
  
    Branch_out      : out std_logic;                            -- Saída do sinal de controle que define quando ocorre Branch 
    Mem_Write_out    : out std_logic;                            -- Saída do sinal de controle que define quando a Memória será escrita
    Mem_Read_out     : out std_logic;                            -- Saída do sinal de controle que define quando a Memória será lida
    Reg_Write_out    : out std_logic;                            -- Saída do sinal de controle que define quando o registrador será escrito
    Mem_To_Reg_out    : out std_logic;                            -- Saída do sinal de controle que define quando um dado será passado da memória para o registrador
    New_PC_out       : out std_logic_vector(31 DOWNTO 0);        -- Soma do PC com imediato (jal) ou reg com imediato substituindo PC (jalr)
    Zero_out        : out std_logic;                            -- Quando o resultado da ALU foi zero (serve para Branch)
    ALU_result_out   : out std_logic_vector(31 DOWNTO 0);        -- Saída do resultado da operação da ALU
    read2_out       : out std_logic_vector(31 DOWNTO 0);        -- Saída do valor lido do read data 2
    Rd_out          : out std_logic_vector(4 DOWNTO 0);          -- Saída da instrução atual buscada na memória de instruções
    Jalr_ou_Jal_out	: out std_logic					    -- Saída que indica se é Jalr ou Jal
    );
END EXMEM;


ARCHITECTURE Behavioral OF EXMEM IS

SIGNAL exmem_sig : std_logic_vector(107 DOWNTO 0);  -- Registrador de 192 bits para armazenar os valores do EXMEM

BEGIN

    PROCESS (clk)
    BEGIN
        IF (rising_edge(clk)) THEN                   -- Detecta a borda de subida do sinal de clock
            exmem_sig(0)    <= Branch_in;          
            exmem_sig(1)    <= Mem_Write_in;          
            exmem_sig(2)   <= Mem_Read_in;      
            exmem_sig(3)   <= Reg_Write_in;
            exmem_sig(4)   <= Mem_To_Reg_in;  
            exmem_sig(36 downto 5)    <= New_PC_in;       
            exmem_sig(37)           <= Zero_in;   
            exmem_sig(69 downto 38)    <= ALU_result_in;   
            exmem_sig(101 downto 70)    <= read2_in;   
            exmem_sig(106 downto 102)    <= Rd_in;   
            exmem_sig(107) <= Jalr_ou_Jal_in;
        END IF;
        IF (falling_edge(clk)) THEN                 -- Detecta a borda de descida do sinal de clock
            Branch_out    <= exmem_sig(0);       
            Mem_Write_out  <= exmem_sig(1);     
            Mem_Read_out  <= exmem_sig(2);      
            Reg_Write_out <= exmem_sig(3);    
            Mem_To_Reg_out <= exmem_sig(4);
            New_PC_out <= exmem_sig(36 downto 5);
            Zero_out <= exmem_sig(37);
            ALU_result_out <= exmem_sig(69 downto 38);
            read2_out <= exmem_sig(101 downto 70);
            Rd_out <= exmem_sig(106 downto 102);
            Jalr_ou_Jal_out <= exmem_sig(107);
        END IF;
    END PROCESS;

    
END Behavioral;s

// VHDL entity Hazard, as the project stores it:
library IEEE;
use IEEE.STD_LOGIC_1164.ALL;

entity Hazard is 
    port( 
        clk                 : IN std_logic;                          -- Entrada do sinal de clock
        Mem_Read_in          : IN std_logic;                          -- Sinal de controle que define quando a Memória será lida
        Rd_EX               : IN std_logic_vector(4 downto 0);       -- Rd é o endereço de destino da operação feita pelo CPU após o estágio de EX
        Rs1, Rs2            : IN std_logic_vector(4 downto 0);       -- Rs1 e Rs2 são os endereços dos registradores contidos na instrução
        stall               : OUT std_logic                          -- Saída que indica se um "stall" (atraso) deve ser aplicado no pipeline
    );
end Hazard;

architecture Behavioral of Hazard is

    signal stall_interno : std_logic := '0';  -- Signal temporário que armazena o nível lógico do stall

begin
    process(clk)
    begin
        if ((Mem_Read_in = '1') and ((Rd_EX = Rs1) or (Rd_EX = Rs2))) then        -- Fórmula do livro, página 322
            stall_interno <= '1';                                                -- Se o sinal de controle de MemRead_in for igual a 1 e o resultado  
        end if;                                                                  -- do estágio de Execution estiver em Rs1 ou Rs2, realiza um stall
    end process;

    stall <= stall_interno;                                                     -- Atribui o valor do signal temporário stall_interno à saída stall

end Behavioral;

// VHDL entity Forward, as the project stores it:
library IEEE;
use IEEE.STD_LOGIC_1164.ALL;

entity Forward is 
    port( 
         clk                        : IN std_logic;                         -- Entrada do sinal de clock
         reg_Write_WB, reg_Write_MEM  : IN std_logic;                         -- Sinais de controle de escrita no registrador do WB e do Mem, respectivamente
         Rs1, Rs2                   : IN std_logic_vector(4 downto 0);      -- Endereçoes dos registradores Rs1 e Rs2 vindos do estágio ID/EX do pipeline
         Rd_WB, Rd_Mem              : IN std_logic_vector(4 downto 0);      -- Endereços dos registradores de armazenamento Rd, vindos dos estágios de MEM/WB e EX/MEM do pipeline
         forward_A, forward_B         : OUT std_logic_vector(1 downto 0)      -- Saídas indicando os forwards para as fontes A e B
     );
end Forward;

ARCHITECTURE Behavioral OF MEMWB IS
    signal forward_A_interno, forward_B_interno : std_logic_vector(1 downto 0) := "00";   -- Sinais internos que armazenam o encaminhamento

begin
    process(clk)
    begin
        if ((reg_Write_MEM = '1') and (not(Rd_Mem = "00000")) and (Rd_Mem = Rs1)) then
            forward_A_interno <= "10";   
        end if;

        if ((reg_Write_MEM = '1') and (not(Rd_Mem = "00000")) and (Rd_Mem = Rs2)) then
            forward_B_interno <= "10";  
        end if;

        if ((reg_Write_WB = '1') and (not(Rd_WB = "00000")) and (Rd_WB = Rs1)) then
            forward_A_interno <= "01";   
        end if;

        if ((reg_Write_WB = '1') and (not(Rd_WB = "00000")) and (Rd_WB = Rs2)) then
            forward_B_interno <= "01";   
        end if;

    end process;

    forward_A <= forward_A_interno;  
    forward_B <= forward_B_interno;
       
END Behavioral;

// VHDL entity MEMWB, as the project stores it:
LIBRARY ieee;
USE ieee.std_logic_1164.all;

ENTITY MEMWB IS
  PORT (
    clk             : IN std_logic;                             -- Entrada do sinal de clock            
    Reg_Write_in     : IN std_logic;                             -- Entrada do sinal de controle que define quando o registrador será escrito
    Mem_To_Reg_in     : IN std_logic;                             -- Entrada do sinal de controle que define quando um dado será passado da memória para o registrador
    Mem_data_in     : IN std_logic_vector(31 DOWNTO 0);         -- Entrada do valor lido na memória
    ALU_result_in    : IN std_logic_vector(31 DOWNTO 0);         -- Entrada do resultado da operação da ALU
    Rd_in           : IN std_logic_vector(4 DOWNTO 0);          -- Entrada da instrução atual buscada na memória de instruções
  
    Reg_Write_out    : out std_logic;                            -- Saída do sinal de controle que define quando o registrador será escrito
    Mem_To_Reg_out    : out std_logic;                            -- Saída do sinal de controle que define quando um dado será passado da memória para o registrador
    Mem_data_out    : out std_logic_vector(31 DOWNTO 0);        -- Saída do valor lido na memória
    ALU_result_out   : out std_logic_vector(31 DOWNTO 0);        -- Saída do resultado da operação da ALU
    Rd_out          : out std_logic_vector(4 DOWNTO 0)          -- Saída da instrução atual buscada na memória de instruções
    );
END MEMWB;


ARCHITECTURE Behavioral OF MEMWB IS

SIGNAL memwb_sig : std_logic_vector(70 DOWNTO 0);  -- Registrador de 70 bits para armazenar os valores do memwb

BEGIN

    PROCESS (clk)
    BEGIN
        IF (rising_edge(clk)) THEN                   -- Detecta a borda de subida do sinal de clock     
            memwb_sig(0)   <= Reg_Write_in;
            memwb_sig(1)   <= Mem_To_Reg_in;  
            memwb_sig(33 downto 2)  <= Mem_data_in ;       
            memwb_sig(65 downto 34)  <= ALU_result_in;   
            memwb_sig(70 downto 66)  <= Rd_in;   
        END IF;
        IF (falling_edge(clk)) THEN                 -- Detecta a borda de descida do sinal de clock
            Reg_Write_out <= memwb_sig(0);    
            Mem_To_Reg_out <= memwb_sig(1);
            Mem_data_out <= memwb_sig(33 downto 2);
            ALU_result_out <= memwb_sig(65 downto 34);
            Rd_out <= memwb_sig(70 downto 66);
        END IF;
    END PROCESS;

    
END Behavioral;
